# Fritzing sketch StepSequencer (saved by Fritzing 0.9.0b)
breadboards: 1

parts:
  Part1 = Arduino Uno (Rev3)
  J1 = Piezo Speaker
  R2 = Resistor [tolerance=±5% resistance=10k package=THT]
  R1 = Photocell (LDR) [package=THT]
  R3 = Rotary Potentiometer (Small) [maximum_resistance=100kΩ package=THT]
  R4 = Rotary Potentiometer (Small) [maximum_resistance=100kΩ package=THT]
  R5 = Rotary Potentiometer (Small) [maximum_resistance=100kΩ package=THT]
  R6 = Rotary Potentiometer (Small) [maximum_resistance=100kΩ package=THT]
  LED1 = LED - 5mm [color="Red (633nm)" package="5 mm [THT]"]
  LED2 = LED - 5mm [color="Red (633nm)" package="5 mm [THT]"]
  LED3 = LED - 5mm [color="Red (633nm)" package="5 mm [THT]"]
  LED4 = LED - 5mm [color="Red (633nm)" package="5 mm [THT]"]
  R7 = Resistor [tolerance=±5% resistance=220 package=THT]
  R8 = Resistor [tolerance=±5% resistance=220 package=THT]
  R9 = Resistor [tolerance=±5% resistance=220 package=THT]
  R10 = Resistor [tolerance=±5% resistance=220 package=THT]

nets:
  N1: Part1.A0, R3.wiper
  N2: Part1.A1, R4.wiper
  N3: Part1.A2, R5.wiper
  N4: Part1.A3, R6.wiper
  N5: Part1.A4/SDA, R2.Pin_1, R1.pin_1
  N6: Part1.D12/MISO, J1.pin2
  N7: Part1.GND, J1.pin1, R2.Pin_0, R3.leg2, R4.leg2, R5.leg2, R6.leg2, R7.Pin_1, R8.Pin_1, R9.Pin_1, R10.Pin_1
  N8: Part1.D2, LED1.anode
  N9: Part1.D3_PWM, LED2.anode
  N10: Part1.D4, LED3.anode
  N11: Part1.D5_PWM, LED4.anode
  N12: Part1.5V, R1.pin_0, R3.leg1, R4.leg1, R5.leg1, R6.leg1
  N13: LED1.cathode, R7.Pin_0
  N14: LED2.cathode, R8.Pin_0
  N15: LED3.cathode, R9.Pin_0
  N16: LED4.cathode, R10.Pin_0
